# Fritzing sketch station météo (saved by Fritzing 0.9.3b)
breadboards: 3

parts:
  Netduino1 = Netduino Plus2
  LCD1 = LCD screen
  R1 = Trimmer Potentiometer [maximum_resistance=10kΩ package=THT]
  R2 = Resistor [tolerance=±5% resistance=220 package=THT]
  LED1 = LED - 5mm [color="Red (633nm)" package="5 mm [THT]"]
  LED2 = LED - 5mm [color="Red (633nm)" package="5 mm [THT]"]
  LED3 = LED - 5mm [color="Red (633nm)" package="5 mm [THT]"]
  R3 = Resistor [tolerance=±5% resistance=220 package=THT]
  R4 = Resistor [tolerance=±5% resistance=220 package=THT]
  R5 = Resistor [tolerance=±5% resistance=220 package=THT]
  A1 = DHT22 module
  IC1 = MQ-2 [package="DIP (Dual Inline) [THT]"]

nets:
  N1: Netduino1.D12_MISO, LCD1.RS
  N2: Netduino1.D11_MOSI, LCD1.E
  N3: Netduino1.D10_PWM3, A1.Out
  N4: Netduino1.D8_CTS1, LED2.cathode
  N5: Netduino1.D7_RTS1, LED3.cathode
  N6: Netduino1.D6_PWM1, LED1.cathode
  N7: Netduino1.D5_PWM0, LCD1.DB4
  N8: Netduino1.D4_CS0, LCD1.DB5
  N9: Netduino1.D3_TX1, LCD1.DB6
  N10: Netduino1.D2_RX1, LCD1.DB7
  +5V: Netduino1.+5V, LCD1.VDD, R1.leg1, R2.Pin_0, A1.+, IC1.pin1
  GND: Netduino1.GND, LCD1.VSS, LCD1.R/W, LCD1.LED-, R1.leg2, R3.Pin_1, R4.Pin_1, R5.Pin_0, A1.-, IC1.pin2
  N11: Netduino1.A0, IC1.pin4
  N12: LCD1.V0, R1.wiper
  N13: LCD1.LED+, R2.Pin_1
  N14: LED1.anode, R3.Pin_0
  N15: LED2.anode, R5.Pin_1
  N16: LED3.anode, R4.Pin_0

custom parts:
  DHT22 module: DHT22 module. Pins VCC Data GND.
  MQ-2: MQ-2 Gas Sensor module
